# Fritzing sketch cc (saved by Fritzing 0.9.9b)
circuit board: 8.46667cm x 5.64444cm
breadboards: 1

parts:
  DHT1 = Humidity and Temperature Sensor DHT11
  元件1 = HC-SR501 Body Sensor Module
  U1 = ESP32S-HiLetgo [part_number=ESP32S-HiLetgo]

nets:
  VCC: DHT1.Vcc, 元件1.VCC, U1.VIN
  N1: DHT1.Data-signal, U1.GPIO16
  GND: DHT1.GND_2, 元件1.GND, U1.GND
  N2: 元件1.OUT, U1.GPIO17

custom parts:
  Humidity and Temperature Sensor DHT11: Digital relative humidity & temperature sensor DHT11
  HC-SR501 Body Sensor Module: Pyroelectric Infrared PIR Motion Sensor Detector Module
  ESP32S-HiLetgo: HiLetgo ESP-WROOM-32 ESP32 ESP-32S Development Board 2.4GHz Dual-Mode WiFi + Bluetooth Dual Cores Microcontroller The ESP32 integrated with Antenna switches, RF Balun, power amplifiers, low-noise amplifiers, filters, and management modules, and the entire solution occupies the least area of PCB. 2.4 GHz Wi-Fi plus Bluetooth dual-mode chip, with TSMC Ultra-low power consumption 40nm technology,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
